// Logisim project 5.3.1.1.circ as structural Verilog: 1 circuit, main circuit main
module main (
  input  A,
  input  B,
  input  C,
  output D
);

  Transistor #(.\type ("n")) transistor_1 (.in(1'b0), .out(D), .gate(A));
  Pull_Resistor #(.pull(1)) pull_resistor_1 (.node(D));
  Transistor #(.\type ("n")) transistor_2 (.in(1'b0), .out(D), .gate(B));
  Transistor #(.\type ("n")) transistor_3 (.in(1'b0), .out(D), .gate(C));
endmodule
