// Logisim project 5.3.1.2.circ as structural Verilog: 1 circuit, main circuit main
module main (
  input  A,
  input  B,
  input  C,
  output D
);

  wire transistor_1_out, transistor_2_out;

  Transistor #(.\type ("n")) transistor_1 (.in(1'b0), .out(transistor_1_out), .gate(A));
  Transistor #(.\type ("n")) transistor_2 (.in(transistor_1_out), .out(transistor_2_out), .gate(B));
  Pull_Resistor #(.pull(1)) pull_resistor_1 (.node(D));
  Transistor #(.\type ("n")) transistor_3 (.in(transistor_2_out), .out(D), .gate(C));
endmodule
