// Logisim project circuit.circ as structural Verilog: 1 circuit, main circuit main
module main (
  input  Input0,
  output Inv3,
  output Inv2,
  output Inv1
);

  Pull_Resistor #(.pull(1)) pull_resistor_1 (.node(Inv3));
  Transistor #(.\type ("n")) transistor_1 (.in(1'b0), .out(Inv3), .gate(Inv2));
  Pull_Resistor #(.pull(1)) pull_resistor_2 (.node(Inv2));
  Transistor #(.\type ("n")) transistor_2 (.in(1'b0), .out(Inv2), .gate(Inv1));
  Pull_Resistor #(.pull(1)) pull_resistor_3 (.node(Inv1));
  Transistor #(.\type ("n")) transistor_3 (.in(1'b0), .out(Inv1), .gate(Input0));
endmodule
